# Fritzing sketch radar connection (saved by Fritzing 0.9.3b)

parts:
  Part2 = Arduino Uno (Rev3) - ICSP
  J1 = Basic Servo
  HC-SR04_Sensor_1 = HC-SR04 Ultrasonic Distance Sensor

nets:
  N1: Part2.D8, HC-SR04_Sensor_1.ECHO
  N2: Part2.D9_PWM, HC-SR04_Sensor_1.TRIG
  N3: Part2.D11_PWM/MOSI, J1.pulse
  3V3: Part2.3V3, J1.vcc
  5V: Part2.5V, HC-SR04_Sensor_1.VCC
  GND: Part2.GND, J1.gnd, HC-SR04_Sensor_1.GND
